# Fritzing sketch tinyjukebox (saved by Fritzing 1.0.1rc)
breadboards: 1

parts:
  LED1 = RGB LED (com. cathode, rgb) [package="5 mm [THT]"]
  R1 = Resistor [tolerance=±5% resistance=330 power=0.25 package=THT]
  R2 = Resistor [tolerance=±5% resistance=2.2k power=0.25 package=THT]
  R3 = Resistor [tolerance=±5% resistance=220 power=0.25 package=THT]
  S1 = Momentary Switch [package=tactile-pth]
  R4 = Resistor [tolerance=±5% resistance=2.2k power=0.25 package=THT]
  S5 = Momentary Switch [package=tactile-pth]
  R6 = Resistor [tolerance=±5% resistance=2.2k power=0.25 package=THT]
  S6 = Momentary Switch [package=tactile-pth]
  R8 = Resistor [tolerance=±5% resistance=2.2k power=0.25 package=THT]
  S7 = Momentary Switch [package=tactile-pth]
  R10 = Resistor [tolerance=±5% resistance=2.2k power=0.25 package=THT]
  S8 = SPST Switch [package=switch-spdt]
  MCU1 = Raspberry Pi Zero
  U1 = mystery part, 3 pins [chip_label="USB Power Bank"]
  U2 = mystery part, 1 pin [chip_label=USB-Socket]
  SP1 = SPEAKER [package=pcb_mount_speaker]
  Q1 = NPN-Transistor [package="TO92 [THT]"]
  U6 = mystery part, 8 pins [chip_label=RFID-RC522]
  R13 = Resistor [tolerance=±5% resistance=4.7k power=0.25 package=THT]
  U8 = mystery part, 2 pins [chip_label="Raspi Power-USB"]
  U10 = mystery part, 8 pins [chip_label="Audio AMP SHIM"]

nets:
  N1: LED1.red_anode, R1.Pin_0, Q1.C
  N2: LED1.common_cathode, S1.3, S5.3, S6.3, S7.3, MCU1.pin_6, MCU1.pin_9, MCU1.pin_39, Q1.E, U6.pin6, U10.pin4
  N3: LED1.green_anode, R2.Pin_0
  N4: LED1.blue_anode, R3.Pin_0
  N5: R1.Pin_1, R4.Pin_0, R6.Pin_0, R8.Pin_0, R10.Pin_0, MCU1.pin_1, MCU1.pin_17, U6.pin8, U10.pin6
  N6: R2.Pin_1, MCU1.pin_13
  N7: R3.Pin_1, MCU1.pin_11
  N8: S1.1, R4.Pin_1, MCU1.pin_31
  N9: S5.1, R6.Pin_1, MCU1.pin_16
  N10: S6.1, R8.Pin_1, MCU1.pin_18
  N11: S7.1, R10.Pin_1, MCU1.pin_22
  N12: S8.P, U8.pin1
  N13: S8.S, U1.pin3
  N14: MCU1.pin_4, U10.pin1
  N15: MCU1.pin_12, U10.pin2
  N16: MCU1.pin_15, R13.Pin_1
  N17: MCU1.pin_19, U6.pin3
  N18: MCU1.pin_21, U6.pin4
  N19: MCU1.pin_23, U6.pin2
  N20: MCU1.pin_24, U6.pin1
  N21: MCU1.pin_29, U6.pin5
  N22: MCU1.pin_35, U10.pin5
  N23: MCU1.pin_37, U6.pin7
  N24: MCU1.pin_40, U10.pin3
  N25: U1.pin1, U2.pin1
  N26: U1.pin2, U8.pin2
  N27: SP1.+, U10.pin7
  N28: SP1.-, U10.pin8
  N29: Q1.B, R13.Pin_0
